// Logisim project displaydriver.circ as structural Verilog: 6 circuits, main circuit main
module main (
  input  [2:0] XR,
  input  [2:0] YR,
  input  TRACE
);

  wire CLOCK_out, RESET_out;
  wire [4:0] dplydriver_1_c0, dplydriver_1_c1, dplydriver_1_c2, dplydriver_1_c3, dplydriver_1_c4;

  Button CLOCK (.out(CLOCK_out));
  Button RESET (.out(RESET_out));
  DotMatrix #(.matrixrows(5), .dotshape("circle")) dotmatrix_1 (
    .col0(dplydriver_1_c0), .col1(dplydriver_1_c1), .col2(dplydriver_1_c2), .col3(dplydriver_1_c3),
    .col4(dplydriver_1_c4));
  DPLYdriver dplydriver_1 (
    .TRACE(TRACE), .XR(XR), .YR(YR), .CLOCK(CLOCK_out), .RESET(RESET_out), .C0(dplydriver_1_c0),
    .C1(dplydriver_1_c1), .C2(dplydriver_1_c2), .C3(dplydriver_1_c3), .C4(dplydriver_1_c4));

  // Notes on the sheet:
  //   Exemple d'utilisation
  //   Réalisation: Frédéric Goualard <Frederic.Goualard@univ-nantes.fr>
  //   Bug connu: le passage de "trace 1" à "trace 0" efface l'écran
  //   Pilote d'affichage pour le projet IrvingOne
  //   V. 1.0
endmodule

module DPLYdriver (
  input  TRACE,
  input  [2:0] XR,
  input  [2:0] YR,
  input  CLOCK,
  input  RESET,
  output [4:0] C0,
  output [4:0] C1,
  output [4:0] C2,
  output [4:0] C3,
  output [4:0] C4
);

  wire [4:0] decextx_1_out0, decextx_1_out1, decextx_1_out2, decextx_1_out3, decextx_1_out4, decexty_1_spany,
       multiplexer_1_out, multiplexer_2_out, multiplexer_3_out, multiplexer_4_out, multiplexer_5_out, NX0,
       NX1, NX2, NX3, NX4, X0out, X1out, X2out, X3out, X4out;

  DecExtX decextx_1 (
    .IN(XR), .OUT0(decextx_1_out0), .OUT1(decextx_1_out1), .OUT2(decextx_1_out2), .OUT3(decextx_1_out3),
    .OUT4(decextx_1_out4), .CLOCK(CLOCK), .RESET(RESET), .TRACE(TRACE));
  Register #(.width(5)) X0 (.D(C0), .Q(X0out), .clk(CLOCK), .clr(RESET));  // open: en
  Register #(.width(5)) X1 (.D(C1), .Q(X1out), .clk(CLOCK), .clr(RESET));  // open: en
  Register #(.width(5)) X2 (.D(C2), .Q(X2out), .clk(CLOCK), .clr(RESET));  // open: en
  assign NX0 = decextx_1_out0 & decexty_1_spany;  // AND_Gate and_1, 5 bits wide
  assign NX1 = decextx_1_out1 & decexty_1_spany;  // AND_Gate and_2, 5 bits wide
  assign NX2 = decextx_1_out2 & decexty_1_spany;  // AND_Gate and_3, 5 bits wide
  assign NX3 = decextx_1_out3 & decexty_1_spany;  // AND_Gate and_4, 5 bits wide
  assign NX4 = decextx_1_out4 & decexty_1_spany;  // AND_Gate and_5, 5 bits wide
  DecExtY decexty_1 (.YR(YR), .CLOCK(CLOCK), .RESET(RESET), .TRACE(TRACE), .spanY(decexty_1_spany));
  Register #(.width(5)) X3 (.D(C3), .Q(X3out), .clk(CLOCK), .clr(RESET));  // open: en
  Register #(.width(5)) X4 (.D(C4), .Q(X4out), .clk(CLOCK), .clr(RESET));  // open: en
  // Probe on NX0
  // Probe on NX1
  // Probe on NX2
  // Probe on NX3
  // Probe on NX4
  Multiplexer #(.width(5), .enable("false")) multiplexer_1 (
    .in0({5{1'b0}}), .in1(X0out), .out(multiplexer_1_out), .sel(TRACE));
  Multiplexer #(.width(5), .enable("false")) multiplexer_2 (
    .in0({5{1'b0}}), .in1(X1out), .out(multiplexer_2_out), .sel(TRACE));
  Multiplexer #(.width(5), .enable("false")) multiplexer_3 (
    .in0({5{1'b0}}), .in1(X2out), .out(multiplexer_3_out), .sel(TRACE));
  Multiplexer #(.width(5), .enable("false")) multiplexer_4 (
    .in0({5{1'b0}}), .in1(X3out), .out(multiplexer_4_out), .sel(TRACE));
  Multiplexer #(.width(5), .enable("false")) multiplexer_5 (
    .in0({5{1'b0}}), .in1(X4out), .out(multiplexer_5_out), .sel(TRACE));
  assign C0 = multiplexer_1_out | NX0;  // OR_Gate or_1, 5 bits wide
  assign C1 = multiplexer_2_out | NX1;  // OR_Gate or_2, 5 bits wide
  assign C2 = multiplexer_3_out | NX2;  // OR_Gate or_3, 5 bits wide
  assign C3 = multiplexer_4_out | NX3;  // OR_Gate or_4, 5 bits wide
  assign C4 = multiplexer_5_out | NX4;  // OR_Gate or_5, 5 bits wide

  // Other names for the same wires on the sheet: X0in[4:0] = C0; X1in[4:0] = C1; X2in[4:0] = C2; X3in[4:0] = C3;
  //   X4in[4:0] = C4
endmodule

module DecExtX (
  input  [2:0] IN,
  input  CLOCK,
  input  RESET,
  input  TRACE,
  output [4:0] OUT0,
  output [4:0] OUT1,
  output [4:0] OUT2,
  output [4:0] OUT3,
  output [4:0] OUT4
);

  wire [2:0] register_1_q;
  wire [4:0] decoder_1_out0, decoder_2_out0, multiplexer_1_out, spanx_1_spanx;

  Decoder #(.select(3), .enable("false")) decoder_1 (
    .out0(decoder_1_out0[0]), .out1(decoder_1_out0[1]), .out2(decoder_1_out0[2]), .out3(decoder_1_out0[3]),
    .out4(decoder_1_out0[4]), .sel(IN));  // open: out5, out6, out7
  Multiplexer #(.width(5), .enable("false")) multiplexer_1 (
    .in0(decoder_1_out0), .in1(decoder_2_out0), .out(multiplexer_1_out), .sel(TRACE));
  Register #(.width(3)) register_1 (.D(IN), .Q(register_1_q), .clk(CLOCK), .clr(RESET));  // open: en
  Decoder #(.select(3), .enable("false")) decoder_2 (
    .out0(decoder_2_out0[0]), .out1(decoder_2_out0[1]), .out2(decoder_2_out0[2]), .out3(decoder_2_out0[3]),
    .out4(decoder_2_out0[4]), .sel(register_1_q));  // open: out5, out6, out7
  spanX spanx_1 (.oldX(multiplexer_1_out), .newX(decoder_1_out0), .spanX(spanx_1_spanx));
  assign OUT0 = {{4{spanx_1_spanx[0]}}, spanx_1_spanx[0]};  // Bit_Extender bit_extender_1
  assign OUT1 = {{4{spanx_1_spanx[1]}}, spanx_1_spanx[1]};  // Bit_Extender bit_extender_2
  assign OUT2 = {{4{spanx_1_spanx[2]}}, spanx_1_spanx[2]};  // Bit_Extender bit_extender_3
  assign OUT3 = {{4{spanx_1_spanx[3]}}, spanx_1_spanx[3]};  // Bit_Extender bit_extender_4
  assign OUT4 = {{4{spanx_1_spanx[4]}}, spanx_1_spanx[4]};  // Bit_Extender bit_extender_5
endmodule

module spanX (
  input  [4:0] oldX,
  input  [4:0] newX,
  output [4:0] spanX
);

  wire comparator_1_gt;
  wire [4:0] dpyspan_1__2x_1, dpyspan_1_not_x_1, dpyspan_2__2x_1, dpyspan_2_not_x_1, multiplexer_1_out,
       multiplexer_2_out;

  DPYspan dpyspan_1 (.x(oldX), ._2x_1(dpyspan_1__2x_1), .not_x_1(dpyspan_1_not_x_1));
  DPYspan dpyspan_2 (.x(newX), ._2x_1(dpyspan_2__2x_1), .not_x_1(dpyspan_2_not_x_1));
  Comparator #(.width(5), .mode("unsigned")) comparator_1 (.a(newX), .b(oldX), .gt(comparator_1_gt));  // open: eq, lt
  Multiplexer #(.width(5), .enable("false")) multiplexer_1 (
    .in0(dpyspan_1__2x_1), .in1(dpyspan_2__2x_1), .out(multiplexer_1_out), .sel(comparator_1_gt));
  Multiplexer #(.width(5), .enable("false")) multiplexer_2 (
    .in0(dpyspan_2_not_x_1), .in1(dpyspan_1_not_x_1), .out(multiplexer_2_out), .sel(comparator_1_gt));
  assign spanX = multiplexer_1_out & multiplexer_2_out;  // AND_Gate and_1, 5 bits wide
endmodule

module DPYspan (
  input  [4:0] x,
  output [4:0] _2x_1,
  output [4:0] not_x_1
);

  wire [4:0] subtractor_1_out;

  Subtractor #(.width(5)) subtractor_1 (.a(x), .b(5'b00001), .out(subtractor_1_out));  // open: bin, bout
  Adder #(.width(5)) adder_1 (.a(x), .b(subtractor_1_out), .out(_2x_1));  // open: cin, cout
  assign not_x_1 = ~subtractor_1_out;  // NOT_Gate not_1, 5 bits wide

  // Notes on the sheet:
  //   Etant donné un nombre binaire de la forme x=2^a (1 seul bit à 1), retourne 2x-1 et not(x-1)
  //   x-1
endmodule

module DecExtY (
  input  [2:0] YR,
  input  CLOCK,
  input  RESET,
  input  TRACE,
  output [4:0] spanY
);

  wire [2:0] register_1_q;
  wire [4:0] decoder_1_out0, decoder_2_out0, multiplexer_1_out;

  Register #(.width(3)) register_1 (.D(YR), .Q(register_1_q), .clk(CLOCK), .clr(RESET));  // open: en
  Decoder #(.select(3), .enable("false")) decoder_1 (
    .out0(decoder_1_out0[0]), .out1(decoder_1_out0[1]), .out2(decoder_1_out0[2]), .out3(decoder_1_out0[3]),
    .out4(decoder_1_out0[4]), .sel(YR));  // open: out5, out6, out7
  Decoder #(.select(3), .enable("false")) decoder_2 (
    .out0(decoder_2_out0[0]), .out1(decoder_2_out0[1]), .out2(decoder_2_out0[2]), .out3(decoder_2_out0[3]),
    .out4(decoder_2_out0[4]), .sel(register_1_q));  // open: out5, out6, out7
  Multiplexer #(.width(5), .enable("false")) multiplexer_1 (
    .in0(decoder_1_out0), .in1(decoder_2_out0), .out(multiplexer_1_out), .sel(TRACE));
  spanX spanx_1 (.oldX(decoder_1_out0), .newX(multiplexer_1_out), .spanX(spanY));
endmodule
