// Logisim project projet_GOMES_KILLIAN.circ as structural Verilog: 7 circuits, main circuit UAL
module UAL (
  input  Input,
  input  [5:0] Rs,
  input  [5:0] Rt,
  output [5:0] Result,
  output [3:0] out_5
);

  wire Rt_Sign, xnor_1_out, xor_1_out;
  wire [4:0] multiplexer_1_out;
  wire [5:0] n2_sc_6bits_1_out_2;

  _2_sC_6bits u_2_sc_6bits_1 (.in_1(Rt), .out_2(n2_sc_6bits_1_out_2));
  Multiplexer #(.width(6), .enable("false")) multiplexer_1 (
    .in0(Rt), .in1(n2_sc_6bits_1_out_2), .out({Rt_Sign, multiplexer_1_out}), .sel(Input));
  Adder #(.width(6)) adder_1 (.a(Rs), .b({Rt_Sign, multiplexer_1_out}), .out(Result), .cout(out_5[1]));  // open: cin
  Comparator #(.width(6), .mode("unsigned")) comparator_1 (
    .a(Result), .b({6{1'b0}}), .eq(out_5[3]), .lt(out_5[2]));  // open: gt
  xor xor_1 (xor_1_out, out_5[2], Rs[5]);
  xnor xnor_1 (xnor_1_out, Rs[5], Rt_Sign);
  and and_1 (out_5[0], xor_1_out, xnor_1_out);

  // Other names for the same wires on the sheet: ctrlUAL = Input; FLAGS[3:0] = out_5; OF = out_5[0]; CF = out_5[1];
  //   SF = out_5[2]; ZF = out_5[3]; RES[5:0] = Result; Rs_Sign = Rs[5]

  // Notes on the sheet:
  //   choice add/sub
  //   operation
  //   getting ZeroFlag & SignFlag
  //   getting CarryFlag
  //   grouping flags
  //   getting the OverflowFlag
  //   Flags are grouped in one Output of 4 bits
endmodule

module _2_sC_6bits (
  input  [5:0] in_1,
  output [5:0] out_2
);

  wire [5:0] not_1_out;

  assign not_1_out = ~in_1;  // NOT_Gate not_1, 6 bits wide
  Adder #(.width(6)) adder_1 (.a(not_1_out), .b(6'b000001), .out(out_2));  // open: cin, cout

  // Notes on the sheet:
  //   2'sC on 6bits
  //   calculus of "Two's complement" of an input on 6 bits
endmodule

module Register_Bank (
  input  [2:0] ri,
  input  regW,
  input  [2:0] rj,
  input  [5:0] val,
  input  Clock,
  input  Reset,
  output [5:0] R_ri,
  output [5:0] R_rj
);

  wire W0, W1, W2, W3, W4, W5, W6, W7;
  wire [5:0] O0, O1, O2, O3, O4, O5, O6, O7;

  Register #(.width(6)) register_1 (.D(val), .en(W0), .Q(O0), .clk(Clock), .clr(Reset));
  Register #(.width(6)) register_2 (.D(val), .en(W1), .Q(O1), .clk(Clock), .clr(Reset));
  Register #(.width(6)) register_3 (.D(val), .en(W2), .Q(O2), .clk(Clock), .clr(Reset));
  Register #(.width(6)) register_4 (.D(val), .en(W3), .Q(O3), .clk(Clock), .clr(Reset));
  Register #(.width(6)) register_5 (.D(val), .en(W4), .Q(O4), .clk(Clock), .clr(Reset));
  Register #(.width(6)) register_6 (.D(val), .en(W5), .Q(O5), .clk(Clock), .clr(Reset));
  Register #(.width(6)) register_7 (.D(val), .en(W6), .Q(O6), .clk(Clock), .clr(Reset));
  Register #(.width(6)) register_8 (.D(val), .en(W7), .Q(O7), .clk(Clock), .clr(Reset));
  Multiplexer #(.select(3), .width(6), .enable("false")) multiplexer_1 (
    .in0(O0), .in1(O1), .in2(O2), .in3(O3), .in4(O4), .in5(O5), .in6(O6), .in7(O7), .out(R_ri), .sel(ri));
  Demultiplexer #(.select(3), .enable("false")) demultiplexer_1 (
    .out0(W0), .out1(W1), .out2(W2), .out3(W3), .out4(W4), .out5(W5), .out6(W6), .out7(W7), .in(regW),
    .sel(ri));
  Multiplexer #(.select(3), .width(6), .enable("false")) multiplexer_2 (
    .in0(O0), .in1(O1), .in2(O2), .in3(O3), .in4(O4), .in5(O5), .in6(O6), .in7(O7), .out(R_rj), .sel(rj));
  // Probe on O0
  // Probe on O1
  // Probe on O2
  // Probe on O3
  // Probe on O4
  // Probe on O5
  // Probe on O6
  // Probe on O7

  // Notes on the sheet:
  //   Inputs
  //   Register Bank
  //   Writing of Ri in the chosen register (depending on regW)
  //   Getting R[ri] & R[rj] from the chosen register
  //   Outputs
  //   Display of the content of the registers
endmodule

module Jump_controler (
  input  [3:0] Opcode,
  input  [3:0] FLAGS,
  output out_3
);

  wire and_1_out, and_2_out, and_3_out, and_4_out;

  and and_1 (and_1_out, Opcode[3], ~Opcode[2], ~Opcode[0], FLAGS[3]);  // AND_Gate
  and and_2 (and_2_out, Opcode[3], ~Opcode[2], ~Opcode[1], Opcode[0], ~FLAGS[3]);  // AND_Gate
  and and_3 (and_3_out, Opcode[3], ~Opcode[2], Opcode[1], ~FLAGS[0], ~FLAGS[3], ~FLAGS[2]);  // AND_Gate
  and and_4 (and_4_out, Opcode[3], ~Opcode[2], Opcode[1], FLAGS[0], ~FLAGS[3], FLAGS[2]);  // AND_Gate
  or or_1 (out_3, and_1_out, and_2_out, and_3_out, and_4_out);

  // Other names for the same wires on the sheet: OF = FLAGS[0]; CF = FLAGS[1]; SF = FLAGS[2]; ZF = FLAGS[3];
  //   NextPCSel = out_3

  // Notes on the sheet:
  //   Inputs : Flags & Opcode
  //   Jump Controler
  //   Output : NextPCSel
endmodule

module Instruction_decoder (
  input  [3:0] Opcode,
  output regW,
  output isLoad,
  output ctrlUAL,
  output XYRen,
  output TRen,
  output ORen,
  output stopClock
);

  and and_1 (regW, ~Opcode[3], Opcode[2], ~Opcode[1]);  // AND_Gate
  and and_2 (isLoad, ~Opcode[3], Opcode[2], ~Opcode[1], ~Opcode[0]);  // AND_Gate
  and and_3 (ctrlUAL, Opcode[3], ~Opcode[2]);  // AND_Gate
  and and_4 (XYRen, ~Opcode[3], ~Opcode[2], ~Opcode[1]);  // AND_Gate
  and and_5 (TRen, ~Opcode[3], Opcode[2], Opcode[1]);  // AND_Gate
  and and_6 (ORen, ~Opcode[3], ~Opcode[2], Opcode[1]);  // AND_Gate
  and and_7 (stopClock, Opcode[3], Opcode[2], Opcode[1], Opcode[0]);

  // Notes on the sheet:
  //   Instruction decoder
  //   Outputs
endmodule

module Register_controler (
  input  [5:0] Ri,
  input  [3:0] Opcode,
  input  XYRen,
  input  [2:0] XR,
  input  [5:0] Imm,
  input  TRen,
  input  [2:0] YR,
  input  ORen,
  input  [1:0] OR,
  output [2:0] out_10,
  output out_11,
  output [2:0] out_12,
  output out_13,
  output out_14,
  output out_15,
  output [1:0] out_16,
  output out_17
);

  wire [2:0] multiplexer_3_out;
  wire [5:0] adder_1_out, bit_extender_1_out, multiplexer_2_out, val_2_prime_sC;
  wire [5:2] val;

  Multiplexer #(.width(6), .enable("false")) multiplexer_1 (
    .in0(Imm), .in1(Ri), .out({val, out_16[1], out_14}), .sel(Opcode[0]));
  _2_sC_6bits u_2_sc_6bits_1 (.in_1({val, out_16[1], out_14}), .out_2(val_2_prime_sC));
  // Probe on {val, out_16[1], out_14}
  // Probe on val_2_prime_sC
  Multiplexer #(.width(6), .enable("false")) multiplexer_2 (
    .in0({val, out_16[1], out_14}), .in1(val_2_prime_sC), .out(multiplexer_2_out), .sel(OR[1]));
  Multiplexer #(.width(3), .enable("false")) multiplexer_3 (.in0(YR), .in1(XR), .out(multiplexer_3_out), .sel(OR[0]));
  assign bit_extender_1_out = {{3{1'b0}}, multiplexer_3_out};  // Bit_Extender bit_extender_1
  Adder #(.width(6)) adder_1 (.a(multiplexer_2_out), .b(bit_extender_1_out), .out(adder_1_out));  // open: cin, cout
  Demultiplexer #(.width(3), .enable("false")) demultiplexer_1 (
    .out0(out_12), .out1(out_10), .in(adder_1_out[2:0]), .sel(OR[0]));
  and and_1 (out_11, XYRen, OR[0]);
  and and_2 (out_13, XYRen, ~OR[0]);  // AND_Gate

  assign out_15 = TRen;
  assign out_16[0] = out_14;
  assign out_17 = ORen;

  // Other names for the same wires on the sheet: _1OPC = Opcode[0]; ORN[1:0] = {out_16[1], out_14}; TRN = out_14;
  //   val[1:0] = {out_16[1], out_14}; XRen = out_11; XRN[2:0] = out_10; YRen = out_13; YRN[2:0] = out_12

  // Notes on the sheet:
  //   Choice between Imm and Ri
  //   Inputs
  //   2'sC of the choice
  //   display of the values
  //   Turtle's Register controler
  //   It changes either x either y
  //   either an add or a sub
  //   new trace and orientation
  //   gives either the new x or the new y
  //   Outputs
endmodule

module Main (
);

  wire and_1_out, CLOCK_out, instruction_decoder_1_ctrlual, instruction_decoder_1_isload,
       instruction_decoder_1_oren, instruction_decoder_1_regw, instruction_decoder_1_stopclock,
       instruction_decoder_1_tren, instruction_decoder_1_xyren, jump_controler_1_out_3,
       register_controler_1_out_11, register_controler_1_out_13, register_controler_1_out_14,
       register_controler_1_out_15, register_controler_1_out_17, RESET_out, TR_q;
  wire [1:0] OR_q, register_controler_1_out_16;
  wire [2:0] register_controler_1_out_10, register_controler_1_out_12, XR_q, YR_q;
  wire [3:0] ual_1_out_5;
  wire [4:0] _1, _2, _3, _4, _5;
  wire [5:0] multiplexer_1_out, register_bank_1_r_ri, register_bank_1_r_rj, ual_1_result;
  wire [7:0] adder_1_out, adder_2_out, adder_3_out, bit_extender_1_out, multiplexer_2_out, PC_q;
  wire [15:0] ram_1_data;

  Button RESET (.out(RESET_out));
  Button CLOCK (.out(CLOCK_out));
  DotMatrix #(.matrixrows(5), .dotshape("circle")) dotmatrix_1 (.col0(_1), .col1(_2), .col2(_3), .col3(_4), .col4(_5));
  Register PC (.D(multiplexer_2_out), .Q(PC_q), .clk(and_1_out), .clr(RESET_out));  // open: en
  RAM #(.dataWidth(16)) ram_1 (.addr(PC_q), .data(ram_1_data), .clk(and_1_out));  // open: sel, ld, clr
  Adder adder_1 (.a(PC_q), .b(8'h1), .out(adder_1_out));  // open: cin, cout
  and and_1 (and_1_out, CLOCK_out, ~instruction_decoder_1_stopclock);  // AND_Gate
  Instruction_decoder instruction_decoder_1 (
    .Opcode(ram_1_data[15:12]), .regW(instruction_decoder_1_regw), .isLoad(instruction_decoder_1_isload),
    .ctrlUAL(instruction_decoder_1_ctrlual), .XYRen(instruction_decoder_1_xyren),
    .TRen(instruction_decoder_1_tren), .ORen(instruction_decoder_1_oren),
    .stopClock(instruction_decoder_1_stopclock));
  Multiplexer #(.width(6), .enable("false")) multiplexer_1 (
    .in0(ual_1_result), .in1(ram_1_data[5:0]), .out(multiplexer_1_out), .sel(instruction_decoder_1_isload));
  assign bit_extender_1_out = {{2{1'b0}}, ram_1_data[5:0]};  // Bit_Extender bit_extender_1
  Adder adder_2 (.a(bit_extender_1_out), .b(8'hc0), .out(adder_2_out));  // open: cin, cout
  Register_Bank register_bank_1 (
    .ri(ram_1_data[11:9]), .regW(instruction_decoder_1_regw), .rj(ram_1_data[8:6]), .val(multiplexer_1_out),
    .R_ri(register_bank_1_r_ri), .R_rj(register_bank_1_r_rj), .Clock(and_1_out), .Reset(RESET_out));
  Adder adder_3 (.a(adder_1_out), .b(adder_2_out), .out(adder_3_out));  // open: cin, cout
  Multiplexer #(.width(8), .enable("false")) multiplexer_2 (
    .in0(adder_1_out), .in1(adder_3_out), .out(multiplexer_2_out), .sel(jump_controler_1_out_3));
  UAL ual_1 (
    .Rs(register_bank_1_r_ri), .Rt(register_bank_1_r_rj), .Result(ual_1_result), .out_5(ual_1_out_5),
    .Input(instruction_decoder_1_ctrlual));
  Register_controler register_controler_1 (
    .Ri(register_bank_1_r_ri), .Opcode(ram_1_data[15:12]), .XYRen(instruction_decoder_1_xyren), .XR(XR_q),
    .Imm(ram_1_data[5:0]), .TRen(instruction_decoder_1_tren), .YR(YR_q), .ORen(instruction_decoder_1_oren),
    .OR(OR_q), .out_10(register_controler_1_out_10), .out_12(register_controler_1_out_12),
    .out_14(register_controler_1_out_14), .out_16(register_controler_1_out_16),
    .out_11(register_controler_1_out_11), .out_13(register_controler_1_out_13),
    .out_15(register_controler_1_out_15), .out_17(register_controler_1_out_17));
  Jump_controler jump_controler_1 (.Opcode(ram_1_data[15:12]), .FLAGS(ual_1_out_5), .out_3(jump_controler_1_out_3));
  Register #(.width(1)) TR (
    .D(register_controler_1_out_14), .en(register_controler_1_out_15), .Q(TR_q), .clk(and_1_out),
    .clr(RESET_out));
  Register #(.width(2)) OR (
    .D(register_controler_1_out_16), .en(register_controler_1_out_17), .Q(OR_q), .clk(and_1_out),
    .clr(RESET_out));
  Register #(.width(3)) YR (
    .D(register_controler_1_out_12), .en(register_controler_1_out_13), .Q(YR_q), .clk(and_1_out),
    .clr(RESET_out));
  Register #(.width(3)) XR (
    .D(register_controler_1_out_10), .en(register_controler_1_out_11), .Q(XR_q), .clk(and_1_out),
    .clr(RESET_out));
  DPLYdriver dplydriver_1 (
    .TRACE(TR_q), .XR(XR_q), .YR(YR_q), .CLOCK(RESET_out), .RESET(and_1_out), .C0(_1), .C1(_2), .C2(_3),
    .C3(_4), .C4(_5));

  // Notes on the sheet:
  //   Display
  //   Memory
  //   Rj
  //   Ri
  //   opcode
  //   regW
  //   isLoad
  //   next instruction
  //   jump
  //   XYRen
  //   TRen
  //   ORen
  //   Opcode
  //   Ri
  //   Imm
endmodule
